// Digital circuit data-path-4-bit-processor-3-24.dig as structural Verilog
module data_path_4_bit_processor_3_24 (
  input  clk,
  input  [1:0] IR_ctrl,
  input  [1:0] Mem_ctrl,
  input  [3:0] Mem_Input,
  output [3:0] PC_Output,
  output [15:0] Instructions_16_bit,
  output [3:0] ALU_out,
  output [3:0] data_1_out,
  output [3:0] data_2_out
);

  wire instr_mem_module_3_24_1_enable_alu;
  wire [7:0] register_file_3_19_1_p6, registerfile_write_ctrl_2_26_1_p2;

  instr_mem_module_3_24 instr_mem_module_3_24_1 (
    .IR_ctrl(IR_ctrl), .pc_ctrl(2'b01), .intr_mem_ctrl(Mem_ctrl), .instr_mem_input(Mem_Input), .clk(clk),
    .ir_output(Instructions_16_bit), .pc_output(PC_Output), .Enable_ALU(instr_mem_module_3_24_1_enable_alu));
  // Register_File_3_19 register_file_3_19_1: pin names not known; wires that end beside it: Instructions_16_bit[5:4], Instructions_16_bit[3:2], clk, ALU_out, Instructions_16_bit[1:0], register_file_3_19_1_p6, data_1_out, data_2_out
  // registerfile_write_ctrl_2_26 registerfile_write_ctrl_2_26_1: pin names not known; wires that end beside it: Instructions_16_bit[1:0], registerfile_write_ctrl_2_26_1_p2
  Multiplexer #(.Bits(8)) multiplexer_1 (
    .sel(instr_mem_module_3_24_1_enable_alu), .in_0(registerfile_write_ctrl_2_26_1_p2), .in_1({8{1'b0}}),
    .out(register_file_3_19_1_p6));
  // ALU_3_19 alu_3_19_1: pin names not known; wires that end beside it: data_1_out, data_2_out, Instructions_16_bit[8:6], ALU_out

  // Notes on the sheet:
  //   Inc A 
  //   0x0
  //   0x4
  //   0x1
  //   0x0
  //   Inc B 
  //   0x5
  //   0x5
  //   0x1
  //   0x0
  //   Add A+B
  //   0x6
  //   0x0
  //   0x0
  //   0x0
  //   Add A+B with Carry
  //   0x6
  //   0x4
  //   0x0
  //   0x0
  //   Sub A-B with borrow
  //   0x6
  //   0x8
  //   0x0
  //   0x0
  //   Sub B-A w borrow
  //   0x2
  //   0x9
  //   0x2
  //   0x0
  //   Sub A, B, C
  //   0x2
  //   0x9
  //   0x0
  //   0x0
  //   Sub B, A, C
  //   0x2
  //   0xD
  //   0x0
  //   0x0
  //   Transfer A
  //   0x0
  //   0x0
  //   0x1
  //   0x0
  //   Decrement A 
  //   0x0
  //   0x8
  //   0x1
  //   0x0
  //   Decrement B
  //   0x5
  //   0x9
  //   0x3
  //   0x0
  //   Transfer B 
  //   0x5
  //   0x1
  //   0x3
  //   0x0
endmodule

/* Test case Test Circuit:
clk IR-ctrl Mem-ctrl Mem-Input PC-Output Instructions-16-bit ALU-out data-1-out  data-2-out
c 0 1 0x0 x x x x x 
c 0 1 0x4 x x x x x 
c 0 1 0x1 x x x x x  
c 0 1 0x0 x x x x x

c 0 1 0x5 x x x x x
c 0 1 0x5 x x x x x 
c 0 1 0x1 x x x x x 
c 0 1 0x0 x x x x x 

c 0 1 0x5 x x x x x
c 0 1 0x5 x x x x x 
c 0 1 0x1 x x x x x 
c 0 1 0x0 x x x x x 

c 0 1 0x2 x x x x x
c 0 1 0xD x x x x x 
c 0 1 0x0 x x x x x 
c 0 1 0x0 x x x x x

c 1 0 0x0 x x x x x 
c 1 0 0x4 x x x x x 
c 1 0 0x1 x x x x x 
c 1 0 0x0 x x x x x 

c 1 0 0x5 x x x x x 
c 1 0 0x5 x x x x x 
c 1 0 0x1 x x x x x 
c 1 0 0x0 x x x x x 

c 1 0 0x5 x x x x x 
c 1 0 0x5 x x x x x 
c 1 0 0x1 x x x x x 
c 1 0 0x0 x x x x x 

c 1 0 0x2 x x x x x 
c 1 0 0xD x x x x x 
c 1 0 0x0 x x x x x 
c 1 0 0x0 x x x x x 
*/
