// Digital circuit instr-mem-module-3-24.dig as structural Verilog
module instr_mem_module_3_24 (
  input  [1:0] IR_ctrl,
  input  [1:0] pc_ctrl,
  input  [1:0] intr_mem_ctrl,
  input  [3:0] instr_mem_input,
  input  clk,
  output [15:0] ir_output,
  output [3:0] pc_output,
  output Enable_ALU
);

  wire and_1_out, not_1_out, not_2_out;
  wire [1:0] demultiplexer_1_out_0, demultiplexer_1_out_1, demultiplexer_1_out_2, demultiplexer_1_out_3;
  wire [3:0] _4_bit_general_purpose_register_1_p5, _4_bit_instruction_register_1_p4,
       _4_bit_instruction_register_2_p4, _4_bit_instruction_register_3_p4, _4_bit_instruction_register_4_p4,
       demultiplexer_2_out_0, demultiplexer_2_out_1, demultiplexer_2_out_2, demultiplexer_2_out_3;

  // _4_Bit_Program_Counter _4_bit_program_counter_1: pin names not known; wires that end beside it: clk, pc_ctrl, pc_output
  // _4_bit_general_purpose_register _4_bit_general_purpose_register_1: pin names not known; wires that end beside it: pc_output, clk, instr_mem_input, intr_mem_ctrl, _4_bit_general_purpose_register_1_p5
  Demultiplexer #(.Selector_Bits(2), .Bits(2)) demultiplexer_1 (
    .sel(pc_output[1:0]), .in(IR_ctrl), .out_0(demultiplexer_1_out_0), .out_1(demultiplexer_1_out_1),
    .out_2(demultiplexer_1_out_2), .out_3(demultiplexer_1_out_3));
  Demultiplexer #(.Selector_Bits(2), .Bits(4)) demultiplexer_2 (
    .sel(pc_output[1:0]), .in(_4_bit_general_purpose_register_1_p5), .out_0(demultiplexer_2_out_0),
    .out_1(demultiplexer_2_out_1), .out_2(demultiplexer_2_out_2), .out_3(demultiplexer_2_out_3));
  // _4_Bit_instruction_register _4_bit_instruction_register_1: pin names not known; wires that end beside it: clk, demultiplexer_2_out_0, demultiplexer_1_out_0, _4_bit_instruction_register_1_p4
  // _4_Bit_instruction_register _4_bit_instruction_register_2: pin names not known; wires that end beside it: clk, demultiplexer_2_out_1, demultiplexer_1_out_1, _4_bit_instruction_register_2_p4
  // _4_Bit_instruction_register _4_bit_instruction_register_3: pin names not known; wires that end beside it: clk, demultiplexer_2_out_2, demultiplexer_1_out_2, _4_bit_instruction_register_3_p4
  // _4_Bit_instruction_register _4_bit_instruction_register_4: pin names not known; wires that end beside it: clk, demultiplexer_2_out_3, demultiplexer_1_out_3, _4_bit_instruction_register_4_p4
  assign ir_output = and_1_out ? {_4_bit_instruction_register_4_p4, _4_bit_instruction_register_3_p4, _4_bit_instruction_register_2_p4, _4_bit_instruction_register_1_p4} : 16'bz;  // Driver driver_1
  not not_1 (not_1_out, pc_output[0]);
  not not_2 (not_2_out, pc_output[1]);
  and and_1 (and_1_out, not_1_out, not_2_out);
  not not_3 (Enable_ALU, and_1_out);
endmodule
